// Logisim project eg1.circ as structural Verilog: 7 circuits, main circuit main
module main (
  input  in_1,
  output out_2,
  output out_3
);

  not not_1 (out_2, out_3);
  not not_2 (out_3, out_2);
endmodule

module \S_R锁存器  (
  input  in_1,
  input  in_2,
  output out_3,
  output out_4
);

  wire or_1_out, or_2_out;

  or or_1 (or_1_out, in_1, out_4);
  or or_2 (or_2_out, out_3, in_2);
  not not_1 (out_3, or_1_out);
  not not_2 (out_4, or_2_out);
endmodule

module \D锁存器  (
  input  CLK,
  input  in_2,
  output out_3,
  output out_4
);

  wire and_1_out, and_2_out, not_1_out;

  and and_1 (and_1_out, CLK, not_1_out);
  not not_1 (not_1_out, in_2);
  and and_2 (and_2_out, CLK, in_2);
  \S_R锁存器  \s_r锁存器_1  (.in_1(and_1_out), .in_2(and_2_out), .out_3(out_3), .out_4(out_4));
endmodule

module \D触发器  (
  input  in_1,
  input  D,
  output Q,
  output out_4
);

  wire \d锁存器_1_out_3 , not_1_out, undriven;

  not not_1 (not_1_out, in_1);
  \D锁存器  \d锁存器_1  (.in_2(D), .out_3(\d锁存器_1_out_3 ), .CLK(not_1_out));  // open: out_4
  \D锁存器  \d锁存器_2  (.in_2(\d锁存器_1_out_3 ), .out_3(Q), .out_4(out_4), .CLK(undriven));
endmodule

module \同步复位  (
  input  D,
  input  reset,
  output Q,
  output out_4
);

  wire and_1_out, clock_1_out, \d锁存器_1_out_3 , not_1_out;

  Clock clock_1 (.out(clock_1_out));
  not not_1 (not_1_out, clock_1_out);
  and and_1 (and_1_out, D, reset);
  \D锁存器  \d锁存器_1  (.in_2(and_1_out), .out_3(\d锁存器_1_out_3 ), .CLK(not_1_out));  // open: out_4
  \D锁存器  \d锁存器_2  (.in_2(\d锁存器_1_out_3 ), .out_3(Q), .out_4(out_4), .CLK(clock_1_out));
endmodule

module \异步复位  (
  input  D,
  input  reset,
  output Q,
  output out_4
);

  wire clock_1_out, \d锁存器_1_out_3 , not_1_out;

  Clock clock_1 (.out(clock_1_out));
  not not_1 (not_1_out, clock_1_out);
  \D锁存器  \d锁存器_1  (.in_2(D), .out_3(\d锁存器_1_out_3 ), .CLK(not_1_out));  // open: out_4
  \D锁存器  \d锁存器_2  (.out_3(Q), .out_4(out_4), .CLK(clock_1_out));  // open: in_2
endmodule

module \搭建寄存器  (
  input  [3:0] in_1
);
endmodule
